# Fritzing sketch Untitled Sketch 2 (saved by Fritzing 1.0.1rc)
circuit board: 8.46667cm x 5.64444cm
breadboards: 1

parts:
  パーツ1 = Arduino Nano (Rev3.0)
  VCC1 = Battery
  U1 = RELAY [package=relay-t9a]
  U2 = RELAY [package=relay-t9a]
  R1 = Resistor [tolerance=±5% power=0.25W resistance=0.1 package=THT]
  R2 = Resistor [tolerance=±5% power=0.25W resistance=0.5 package=THT]
  U3 = RELAY [package=relay-t9a]
  R3 = Resistor [tolerance=±5% power=0.25W resistance=10k package=THT]
  R4 = Resistor [tolerance=±5% power=0.25W resistance=10k package=THT]
  U4 = RELAY [package=relay-t9a]
  U5 = RELAY [package=relay-t9a]
  R5 = Resistor [tolerance=±5% power=0.25W resistance=0.5 package=THT]
  R6 = Resistor [tolerance=±5% power=0.25W resistance=0.5 package=THT]
  IC1 = Voltage Regulator [package=to-92]
  C1 = Ceramic Capacitor [capacitance=0.1µF voltage=35V package="1206 [SMD, multilayer]"]
  C2 = Ceramic Capacitor [capacitance=0.33µF voltage=35V package="1206 [SMD, multilayer]"]

nets:
  GND: パーツ1.GND, パーツ1.A1, VCC1.-, R1.Pin_1, R2.Pin_1, R3.Pin_0, R5.Pin_1, R6.Pin_1, C1.0, C2.1
  N1: パーツ1.D3, U1.COIL2
  N2: パーツ1.D4, U2.COIL2
  N3: パーツ1.D5, U4.COIL2
  N4: パーツ1.D6, U5.COIL2
  N5: パーツ1.D7, U3.COIL2
  N6: パーツ1.5V, U1.COIL1, U2.COIL1, U3.COIL1, U4.COIL1, U5.COIL1, IC1.IN, C2.0
  N7: パーツ1.A0, R3.Pin_1, R4.Pin_0
  N8: パーツ1.AREF, IC1.OUT, C1.1
  N9: VCC1.+, U1.MAIN, U2.MAIN, U3.MAIN, U4.MAIN, U5.MAIN
  N10: U1.NO, R1.Pin_0
  N11: U2.NO, R2.Pin_0
  N12: U3.NO, R4.Pin_1
  N13: U4.NO, R5.Pin_0
  N14: U5.NO, R6.Pin_0
