# Fritzing sketch sma_switcher (saved by Fritzing 1.0.1rc)
circuit board: 10.7796cm x 6.66733cm
breadboards: 1

parts:
  パーツ1 = Arduino Nano (Rev3.0)
  R1 = Resistor [tolerance=±5% power=0.25W resistance=1k package=THT]
  Q1 = Basic FET N-Channel [package="TO220 [THT]"]
  R2 = Resistor [tolerance=±5% power=0.25W resistance=1k package=THT]
  R3 = Resistor [tolerance=±5% power=0.25W resistance=1k package=THT]
  R4 = Resistor [tolerance=±5% power=0.25W resistance=1k package=THT]
  Q2 = Basic FET N-Channel [package="TO220 [THT]"]
  Q3 = Basic FET N-Channel [package="TO220 [THT]"]
  Q4 = Basic FET N-Channel [package="TO220 [THT]"]
  R5 = Resistor [tolerance=±5% power=0.25W resistance=10k package=THT]
  R6 = Resistor [tolerance=±5% power=0.25W resistance=10k package=THT]
  R7 = Resistor [tolerance=±5% power=0.25W resistance=10k package=THT]
  R8 = Resistor [tolerance=±5% power=0.25W resistance=10k package=THT]
  U1 = RELAY [package=relay-g5q]
  U2 = RELAY [package=relay-g5q]
  U3 = RELAY [package=relay-g5q]
  U4 = RELAY [package=relay-g5q]
  R9 = Resistor [tolerance=±5% power=0.25W resistance=100 package=THT]
  LED1 = LEDs [package=led10mm]
  LED2 = LEDs [package=led10mm]
  LED3 = LEDs [package=led10mm]
  LED4 = LEDs [package=led10mm]
  LED5 = LEDs [package=led10mm]
  LED6 = LEDs [package=led10mm]
  LED7 = LEDs [package=led10mm]
  LED8 = LEDs [package=led10mm]
  R10 = Resistor [tolerance=±5% power=0.25W resistance=10k package=THT]
  LED9 = LEDs [package=led10mm]

nets:
  GND: パーツ1.GND, Q1.source, Q2.source, Q3.source, Q4.source, R5.Pin_1, R6.Pin_1, R7.Pin_1, R8.Pin_1, LED1.C, LED2.C, LED3.C, LED4.C, LED5.C, LED6.C, LED7.C, LED8.C
  N1: パーツ1.D2, R4.Pin_0
  N2: パーツ1.D3, R3.Pin_0
  N3: パーツ1.D4, R2.Pin_0
  N4: パーツ1.D5, R1.Pin_0
  N5: パーツ1.D10, LED9.C
  5V: パーツ1.5V, U1.COIL1, U2.COIL1, U3.COIL1, U4.COIL1, R9.Pin_0, R10.Pin_0
  N6: R1.Pin_1, Q1.gate, R5.Pin_0
  N7: Q1.drain, U1.COIL2
  N8: R2.Pin_1, Q2.gate, R6.Pin_0
  N9: R3.Pin_1, Q3.gate, R7.Pin_0
  N10: R4.Pin_1, Q4.gate, R8.Pin_0
  N11: Q2.drain, U2.COIL2
  N12: Q3.drain, U3.COIL2
  N13: Q4.drain, U4.COIL2
  N14: U1.MAIN, U2.MAIN, U3.MAIN, U4.MAIN, R9.Pin_1
  N15: U1.NO, LED2.A
  N16: U1.NC, LED1.A
  N17: U2.NO, LED4.A
  N18: U2.NC, LED3.A
  N19: U3.NO, LED6.A
  N20: U3.NC, LED5.A
  N21: U4.NO, LED8.A
  N22: U4.NC, LED7.A
  N23: R10.Pin_1, LED9.A
