# Fritzing sketch tempcontrolboard2 (saved by Fritzing 0.9.3b)
circuit board: 10cm x 6cm
perfboards: 2

parts:
  パーツ1 = Arduino Nano (Rev3.0)
  To_BD_CN7 = Screw terminal - 2 pins [package=THT]
  R1 = Resistor [tolerance=±5% resistance=1k package=THT]
  S1 = Round Pushbutton
  S2 = Round Pushbutton
  IC1 = IC, SIP package, 10 pins [chip_label="SB1602 I2C LCD"]
  U1 = TLP621 [package=THT]
  J1 = Screw terminal - 2 pins [package=THT]
  R2 = Temperature Sensor (Thermistor) [package=THT]
  R3 = Resistor [tolerance=±5% resistance=20k package=THT]
  J2 = Screw terminal - 2 pins [package=THT]
  C1 = Ceramic Capacitor [capacitance=100nF package="100 mil [THT, multilayer]"]

nets:
  N1: パーツ1.GND, S1.leg1, S2.leg1, IC1.pin4, U1.Pin_2, R3.Pin_0, J2.pin1, C1.1
  N2: パーツ1.D5, R1.Pin_0
  N3: パーツ1.D6, S1.leg0
  N4: パーツ1.D7, S2.leg0
  N5: パーツ1.VIN, J2.pin2
  N6: パーツ1.5V, IC1.pin1, IC1.pin5
  N7: パーツ1.A5, IC1.pin2
  N8: パーツ1.A4, IC1.pin3
  N9: パーツ1.A1, J1.pin2, R2.pin_0, R3.Pin_1, C1.0
  N10: パーツ1.A0, パーツ1.AREF, パーツ1.3V3, J1.pin1, R2.pin_1
  N11: To_BD_CN7.pin1, U1.Pin_4
  N12: To_BD_CN7.pin2, U1.Pin_3
  N13: R1.Pin_1, U1.Pin_1

custom parts:
  Temperature Sensor (Thermistor): A 20k NTC Thermistor (Temperature Sensor)
