# Fritzing sketch powersource_vreg (saved by Fritzing 0.9.3b)
breadboards: 1
perfboards: 1

parts:
  J_USBin = USB micro B connector [form="♂ (male)" package=THT]
  C1 = Electrolytic Capacitor [capacitance=47µF package="100 mil [THT, electrolytic]"]
  D1 = Zener Diode [part_number=1N4732A breakdown_voltage=5.1V package="300 mil [THT]"]
  S_5Vtoggle = Toggle Switch [package=THT]
  S_RegToggle = Toggle Switch [package=THT]
  J_5VTerm = Screw terminal - 2 pins [package=THT]
  J_RegTerm = Screw terminal - 2 pins [package=THT]
  D2 = Zener Diode [part_number=1N4732A breakdown_voltage=5.1V package="300 mil [THT]"]
  LED1 = LED - 5mm [color="Red (633nm)" package="5 mm [THT]"]
  R1 = Resistor [tolerance=±5% resistance=1k package=THT]
  S_5Vtact = Pushbutton [package="[THT]"]
  JP_5Vmale = Header 2 [package=molex-1x2_lock]
  J_5Vfemale = female pin header, 2 pins [form="♀ (female)"]
  D3 = Zener Diode [part_number=1N4732A breakdown_voltage=5.1V package="300 mil [THT]"]
  IN- = male pin header, 1 pin [form="♂ (male)"]
  IN+ = male pin header, 1 pin [form="♂ (male)"]
  OUT+ = male pin header, 1 pin [form="♂ (male)"]
  OUT- = male pin header, 1 pin [form="♂ (male)"]
  J_Vmeter = male pin header, 3 pins [form="♂ (male)"]
  S_RegTact = Pushbutton [package="[THT]"]
  J_RegFemale = female pin header, 2 pins [form="♀ (female)"]
  JP_RegMale = Header 2 [package=molex-1x2_lock]
  S_MeasSEL = Toggle Switch [package=THT]
  J_ExtMeasIN = female pin header, 2 pins [form="♀ (female)"]
  LED2 = LED - 5mm [color="Red (633nm)" package="5 mm [THT]"]
  R2 = Resistor [tolerance=±5% resistance=680 package=THT]

nets:
  N1: J_USBin.pin1, C1.+, D1.cathode, S_5Vtoggle.COM, S_5Vtact.Pin_3, IN+.pin1, J_Vmeter.pin2
  N2: J_USBin.pin5, C1.-, D1.anode, J_5VTerm.pin2, J_RegTerm.pin2, D2.anode, R1.Pin_0, JP_5Vmale.1, J_5Vfemale.pin1, D3.anode, IN-.pin1, OUT-.pin1, J_Vmeter.pin1, J_RegFemale.pin1, JP_RegMale.1, R2.Pin_0
  N3: S_5Vtoggle.L2, J_5VTerm.pin1, D2.cathode, LED1.anode, S_5Vtact.Pin_1, JP_5Vmale.2, J_5Vfemale.pin2
  N4: S_RegToggle.COM, OUT+.pin1, S_RegTact.Pin_3, S_MeasSEL.L2
  N5: S_RegToggle.L2, J_RegTerm.pin1, D3.cathode, S_RegTact.Pin_1, S_RegTact.Pin_2, J_RegFemale.pin2, JP_RegMale.2, LED2.anode
  N6: LED1.cathode, R1.Pin_1
  N7: J_Vmeter.pin3, S_MeasSEL.COM
  N8: S_MeasSEL.L1, J_ExtMeasIN.pin1, J_ExtMeasIN.pin2
  N9: LED2.cathode, R2.Pin_1

notes:
  DC-DC Stepdown
  Converter
  LED Voltage Meter
  MAX 5V 2A
  5V OUT
  Regurator OUT
