# Fritzing sketch usbswitch (saved by Fritzing 0.9.3b)
circuit board: 8.73614cm x 5.81286cm
circuit board: 5.39695cm x 8.77156cm
circuit board: 9.04905cm x 5.25416cm
perfboards: 2
breadboards: 1

parts:
  J3 = USB micro B connector [form="♂ (male)" package=THT]
  Pro_Micro1 = Pro Micro
  K2 = Camdenboss CTB0158-3 [part_number=CTB0158-3 package=THT]
  K3 = Camdenboss CTB0158-3 [part_number=CTB0158-3 package=THT]
  K4 = Camdenboss CTB0158-3 [part_number=CTB0158-3 package=THT]
  K1 = Camdenboss CTB0158-3 [part_number=CTB0158-3 package=THT]
  J8 = male pin header, 6 pins [form="♂ (male)"]
  J9 = Screw terminal - 2 pins [package=THT]
  J10 = Screw terminal - 2 pins [package=THT]
  J12 = USB micro B connector [form="♂ (male)" package=THT]
  C1 = Electrolytic Capacitor [capacitance=47µF package="100 mil [THT, electrolytic]"]
  Q1 = Basic FET P-Channel [package="TO220 [THT]"]
  U1 = Voltage Regulator - 3.3V [package="TO220 [THT]"]
  C2 = Electrolytic Capacitor [capacitance=47µF package="100 mil [THT, electrolytic]"]
  C3 = Ceramic Capacitor [capacitance=100nF package="100 mil [THT, multilayer]"]
  D3 = Zener Diode [part_number=1N4732A breakdown_voltage=3.3V package="300 mil [THT]"]
  D2 = Zener Diode [part_number=1N4732A breakdown_voltage=5.1V package="300 mil [THT]"]
  R1 = Resistor [tolerance=±5% resistance=100k package=THT]
  R2 = Resistor [tolerance=±5% resistance=1k package=THT]
  LED1 = LED - 5mm [color="Red (633nm)" package="5 mm [THT]"]
  D1 = Zener Diode [part_number=1N4732A breakdown_voltage=5.1V package="300 mil [THT]"]
  R3 = Resistor [tolerance=±5% resistance=1k package=THT]
  R4 = Resistor [tolerance=±5% resistance=330 package=THT]
  LED2 = LED - 5mm [color="Green (570nm)" package="5 mm [THT]"]
  R5 = Resistor [tolerance=±5% resistance=1k package=THT]
  LED3 = LED - 5mm [color="Yellow (595nm)" package="5 mm [THT]"]
  LED4 = LED - 5mm [color="Green (570nm)" package="5 mm [THT]"]
  D4 = Zener Diode [part_number=1N4732A breakdown_voltage=3.3V package="300 mil [THT]"]
  S1 = Toggle Switch [package=THT]
  J11 = single row smd male pin header, 5 pins [form="♂ (male)"]

nets:
  Relay VCC: J3.pin1, Pro_Micro1.VCC, K1.pin2, J8.pin1, C1.+, Q1.source, R1.Pin_1, D1.cathode, R5.Pin_0
  Relay GND: J3.pin5, Pro_Micro1.GND, J8.pin6, J9.pin2, J10.pin2, C1.-, U1.GND, C2.-, C3.1, D3.anode, D2.anode, LED1.cathode, D1.anode, LED2.cathode, D4.anode, S1.COM
  N1: Pro_Micro1.D5, J8.pin2
  N2: Pro_Micro1.D6, J8.pin3
  N3: Pro_Micro1.D7, J8.pin4
  N4: Pro_Micro1.D8, J8.pin5
  N5: Pro_Micro1.D9, R2.Pin_0
  N6: Pro_Micro1.D10, LED3.cathode
  N7: Pro_Micro1.D16/MOSI, LED4.cathode
  N8: Pro_Micro1.D15/SCLK, S1.L2
  N9: K2.pin1, J12.pin2
  N10: K2.pin2, J11.pin3
  N11: K3.pin1, J12.pin3
  N12: K3.pin2, J11.pin2
  N13: K4.pin1, J12.pin4
  N14: K4.pin2, J11.pin1
  5V OUT: K1.pin3, J9.pin1, D2.cathode, R3.Pin_1
  3.3V OUT: J10.pin1, U1.output_voltage, C2.+, D3.cathode, R4.Pin_1, D4.cathode
  N15: J12.pin1, J11.pin5
  N16: Q1.gate, R1.Pin_0, R2.Pin_1
  N17: Q1.drain, U1.input_voltage, C3.0
  N18: LED1.anode, R3.Pin_0
  N19: R4.Pin_0, LED2.anode
  N20: R5.Pin_1, LED3.anode, LED4.anode

notes:
  VCC RL4 RL3 RL2 RL1 GND
  K4(D+) K3(D-) K2(VCC) K1(5V)
  Noff-C-Non
  USB Power IN
  USB Control IN
  5V OUT
  3.3V OUT
  USB HOST
  USB DEVICE
  to Relay Module
  USB Control

custom parts:
  Pro Micro: The SparkFun Pro Micro is a complete USB-based microcontoller development system, in a very small footprint, capable of implementing many types of projects. All programming can be done via the USB port.
